# Fritzing sketch Project 3 Layout (saved by Fritzing 0.9.4)
breadboards: 2

parts:
  Part1 = Arduino Uno (Rev3)
  Part2 = Arduino Uno (Rev3)
  NEOPIXEL1 = Neopixel Strip -- White (30/m) [part_number=1376]
  Part3 = 9-DOF Absolute Orientation IMU Fusion Breakout - BNO055
  S1 = Pushbutton [package="[SMD]"]
  S2 = Pushbutton [package="[SMD]"]
  R1 = Resistor [tolerance=±5% resistance=220 package=THT]

nets:
  N1: Part1.A4/SDA, Part2.A4/SDA, Part3.SDA_5V
  N2: Part1.A5/SCL, Part2.A5/SCL, Part3.SCL_5V
  N3: Part1.D8, Part2.D8
  GND: Part1.GND, Part2.GND, NEOPIXEL1.GND, Part3.GND, S2.Pin_1, S2.Pin_2, R1.Pin_1
  N4: Part1.D2, NEOPIXEL1.Din
  N5: Part1.D4, S2.Pin_3, S2.Pin_4
  5V: Part1.5V, NEOPIXEL1.+5V, Part3.5.0V
  N6: Part2.D12/MISO, S1.Pin_1, S1.Pin_2, R1.Pin_0
  N7: Part2.5V, S1.Pin_3, S1.Pin_4

custom parts:
  Neopixel Strip -- White (30/m): These NeoPixel strips have 30 digitally-addressable pixel LEDs per meter and are very affordable and are only 12.5 mm wide, 10 mm if you remove the strip from the casing.
  9-DOF Absolute Orientation IMU Fusion Breakout - BNO055: A MEMS accelerometer, magnetometer and gyroscope on a single die with a high speed ARM Cortex-M0 based processor to digest all the sensor data, abstract the sensor fusion and real time requirements away, and spit out data you can use in quaternions, Euler angles or vectors.
